// Logisim project lab10part1_1.circ as structural Verilog: 2 circuits, main circuit main
module main (
  input  Clear,
  output A,
  output B
);

  wire clock_1_out, or_1_out;

  Clock clock_1 (.out(clock_1_out));
  or or_1 (or_1_out, A, B);
  J_K_Flip_Flop j_k_ff_1 (
    .J(or_1_out), .clk(clock_1_out), .K(1'b0), .Q(A), .en(1'b1), .reset(Clear));  // open: Qn, preset
  J_K_Flip_Flop j_k_ff_2 (
    .J(1'b1), .clk(clock_1_out), .K(or_1_out), .Q(B), .en(1'b1), .reset(Clear));  // open: Qn, preset
endmodule

module HalloPolis (
  input  in_1,
  input  in_2,
  output A,
  output B
);

  wire clock_1_out, nor_1_out, or_1_out;

  Clock clock_1 (.out(clock_1_out));
  or or_1 (or_1_out, A, B);
  J_K_Flip_Flop j_k_ff_1 (
    .J(1'b1), .clk(clock_1_out), .K(or_1_out), .Q(A), .en(in_1), .reset(in_2));  // open: Qn, preset
  nor nor_1 (nor_1_out, A, B);
  J_K_Flip_Flop j_k_ff_2 (
    .J(1'b0), .clk(clock_1_out), .K(nor_1_out), .Q(B), .en(in_1), .reset(in_2));  // open: Qn, preset
endmodule
